# Fritzing sketch pcb (saved by Fritzing 0.9.3b)
circuit board: 15.24cm x 15.24cm
breadboards: 1

parts:
  J5 = female pin header, 8 pins [form="♀ (female)"]
  J6 = female pin header, 8 pins [form="♀ (female)"]
  JP2 = Header 5x2 [package=avr_icsp]
  J7 = male pin header, 10 pins [form="♂ (male)"]
  J8 = male pin header, 10 pins [form="♂ (male)"]
  Pro_Micro1 = SparkFun Pro Micro
  JP5 = Header 5x2 [package=avr_icsp]
  J17 = female pin header, 8 pins [form="♀ (female)"]
  J18 = male pin header, 16 pins [form="♂ (male)"]
  J19 = female pin header, 8 pins [form="♀ (female)"]
  J20 = male pin header, 16 pins [form="♂ (male)"]
  J21 = female pin header, 8 pins [form="♀ (female)"]
  J22 = female pin header, 8 pins [form="♀ (female)"]
  JP6 = Header 5x2 [package=avr_icsp]
  J23 = male pin header, 10 pins [form="♂ (male)"]
  J24 = male pin header, 10 pins [form="♂ (male)"]
  J25 = female pin header, 8 pins [form="♀ (female)"]
  J26 = male pin header, 16 pins [form="♂ (male)"]
  J27 = female pin header, 8 pins [form="♀ (female)"]
  J28 = female pin header, 8 pins [form="♀ (female)"]
  JP7 = Header 5x2 [package=avr_icsp]
  J29 = male pin header, 10 pins [form="♂ (male)"]
  J30 = male pin header, 10 pins [form="♂ (male)"]
  J31 = female pin header, 8 pins [form="♀ (female)"]
  J32 = male pin header, 16 pins [form="♂ (male)"]
  J33 = female pin header, 8 pins [form="♀ (female)"]
  J34 = female pin header, 8 pins [form="♀ (female)"]
  JP8 = Header 5x2 [package=avr_icsp]
  J35 = male pin header, 10 pins [form="♂ (male)"]
  J36 = male pin header, 10 pins [form="♂ (male)"]
  C1 = Ceramic Capacitor [capacitance=100nF package="100 mil [THT, multilayer]"]
  C2 = Ceramic Capacitor [capacitance=100nF package="100 mil [THT, multilayer]"]
  C3 = Ceramic Capacitor [capacitance=100nF package="100 mil [THT, multilayer]"]
  0_1uF = Ceramic Capacitor [capacitance=100nF package="100 mil [THT, multilayer]"]

nets:
  N1: J5.pin1, J18.pin2
  N2: J5.pin2, J18.pin1
  N3: J5.pin3, J18.pin3
  N4: J5.pin4, J18.pin4
  N5: J5.pin5, J18.pin5
  N6: J5.pin6, J18.pin6
  N7: J5.pin7, J18.pin7
  N8: J5.pin8, J18.pin8
  N9: J6.pin1, J18.pin15
  N10: J6.pin2, J18.pin16
  N11: J6.pin3, J18.pin14
  N12: J6.pin4, J18.pin13
  N13: J6.pin5, J18.pin12
  N14: J6.pin6, J18.pin11
  N15: J6.pin7, J18.pin10
  N16: J6.pin8, J18.pin9
  N17: JP2.1, J8.pin1, J8.pin2, J8.pin3, J8.pin4, J8.pin5, J8.pin6, J8.pin7, J8.pin8, J8.pin9, J8.pin10, J17.pin1, 0_1uF.0
  N18: JP2.2, J7.pin1, J7.pin2, J7.pin3, J7.pin4, J7.pin5, J7.pin6, J7.pin7, J7.pin8, J7.pin9, J7.pin10, J17.pin2, 0_1uF.1
  N19: JP2.4, J17.pin4
  N20: JP2.6, J17.pin5
  N21: JP2.8, J17.pin6
  N22: JP2.9, J17.pin8
  N23: JP2.10, J17.pin7
  N24: Pro_Micro1.GND, JP5.1
  N25: Pro_Micro1.10, JP5.10
  N26: Pro_Micro1.16, JP5.8
  N27: Pro_Micro1.14, JP5.6
  N28: Pro_Micro1.15, JP5.4
  N29: Pro_Micro1.A0, JP5.9
  N30: Pro_Micro1.A1, JP5.7
  N31: Pro_Micro1.A2, JP5.5
  N32: Pro_Micro1.A3, JP5.3
  N33: Pro_Micro1.VCC, JP5.2
  N34: J19.pin1, JP6.1, J24.pin1, J24.pin2, J24.pin3, J24.pin4, J24.pin5, J24.pin6, J24.pin7, J24.pin8, J24.pin9, J24.pin10, C1.0
  N35: J19.pin2, JP6.2, J23.pin1, J23.pin2, J23.pin3, J23.pin4, J23.pin5, J23.pin6, J23.pin7, J23.pin8, J23.pin9, J23.pin10, C1.1
  N36: J19.pin4, JP6.4
  N37: J19.pin5, JP6.6
  N38: J19.pin6, JP6.8
  N39: J19.pin7, JP6.10
  N40: J19.pin8, JP6.7
  N41: J20.pin1, J22.pin2
  N42: J20.pin2, J22.pin1
  N43: J20.pin3, J22.pin3
  N44: J20.pin4, J22.pin4
  N45: J20.pin5, J22.pin5
  N46: J20.pin6, J22.pin6
  N47: J20.pin7, J22.pin7
  N48: J20.pin8, J22.pin8
  N49: J20.pin9, J21.pin8
  N50: J20.pin10, J21.pin7
  N51: J20.pin11, J21.pin6
  N52: J20.pin12, J21.pin5
  N53: J20.pin13, J21.pin4
  N54: J20.pin14, J21.pin3
  N55: J20.pin15, J21.pin1
  N56: J20.pin16, J21.pin2
  N57: J25.pin1, JP7.1, J30.pin1, J30.pin2, J30.pin3, J30.pin4, J30.pin5, J30.pin6, J30.pin7, J30.pin8, J30.pin9, J30.pin10, C2.0
  N58: J25.pin2, JP7.2, J29.pin1, J29.pin2, J29.pin3, J29.pin4, J29.pin5, J29.pin6, J29.pin7, J29.pin8, J29.pin9, J29.pin10, C2.1
  N59: J25.pin4, JP7.4
  N60: J25.pin5, JP7.6
  N61: J25.pin6, JP7.8
  N62: J25.pin7, JP7.10
  N63: J25.pin8, JP7.3
  N64: J26.pin1, J28.pin2
  N65: J26.pin2, J28.pin1
  N66: J26.pin3, J28.pin3
  N67: J26.pin4, J28.pin4
  N68: J26.pin5, J28.pin5
  N69: J26.pin6, J28.pin6
  N70: J26.pin7, J28.pin7
  N71: J26.pin8, J28.pin8
  N72: J26.pin9, J27.pin8
  N73: J26.pin10, J27.pin7
  N74: J26.pin11, J27.pin6
  N75: J26.pin12, J27.pin5
  N76: J26.pin13, J27.pin4
  N77: J26.pin14, J27.pin3
  N78: J26.pin15, J27.pin1
  N79: J26.pin16, J27.pin2
  N80: J31.pin1, JP8.1, J36.pin1, J36.pin2, J36.pin3, J36.pin4, J36.pin5, J36.pin6, J36.pin7, J36.pin8, J36.pin9, J36.pin10, C3.0
  N81: J31.pin2, JP8.2, J35.pin1, J35.pin2, J35.pin3, J35.pin4, J35.pin5, J35.pin6, J35.pin7, J35.pin8, J35.pin9, J35.pin10, C3.1
  N82: J31.pin4, JP8.4
  N83: J31.pin5, JP8.6
  N84: J31.pin6, JP8.8
  N85: J31.pin7, JP8.10
  N86: J31.pin8, JP8.5
  N87: J32.pin1, J34.pin2
  N88: J32.pin2, J34.pin1
  N89: J32.pin3, J34.pin3
  N90: J32.pin4, J34.pin4
  N91: J32.pin5, J34.pin5
  N92: J32.pin6, J34.pin6
  N93: J32.pin7, J34.pin7
  N94: J32.pin8, J34.pin8
  N95: J32.pin9, J33.pin8
  N96: J32.pin10, J33.pin7
  N97: J32.pin11, J33.pin6
  N98: J32.pin12, J33.pin5
  N99: J32.pin13, J33.pin4
  N100: J32.pin14, J33.pin3
  N101: J32.pin15, J33.pin1
  N102: J32.pin16, J33.pin2

custom parts:
  SparkFun Pro Micro: The Pro Micro is similar to the Pro Mini except with an ATmega32U4 on board. The USB transceiver inside the 32U4 allows us to add USB connectivity on-board and do away with bulky external USB interface. Based on: https://github.com/unorthodox-engineers/unorthodox-arduino/blob/master/Unorthodox/fritzing/parts/Pro%20Micro.fzpz
